// Logisim project miniCPU.circ as structural Verilog: 6 circuits, main circuit main
module main (
  input  En_Hardcode,
  input  [31:0] Hardcoded_Data_32_bit,
  input  [7:0] Hardcoded_Address_8_bit,
  input  [31:0] Hardcoded_Reg_Val_32_bit,
  input  [2:0] Hardcoded_Reg_Add_3_bit,
  input  Memory_Trigger,
  input  Register_Trigger
);

  wire and_1_out, and_2_out, and_3_out, CLEAR_CU, CLEAR_MEMORY, CLEAR_Reg, CLEAR_REG_FILE, CLOCK_out,
       control_unit_1_inter, EN_IMMEDIATE, EN_MEM_DATA, EN_RM, EN_WRITE, INTERRUPT, multiplexer_1_out,
       not_2_out, not_3_out, or_1_out, or_3_out, or_4_out, or_5_out, or_6_out, RESET_CLOCK, STAGE_1, STAGE_2,
       STAGE_3, STAGE_4, STAGE_5;
  wire [2:0] multiplexer_5_out, OP_TYPE, RA_ADDRESS, RB_ADDRESS, RY_ADDRESS;
  wire [3:0] OPCODE;
  wire [7:0] bit_extender_3_out, MEM_ADDRESS;
  wire [15:0] instruction_register_1_immdeiate;
  wire [31:0] adder_1_out, alu_1_rz, bit_extender_1_out, IMMEDIATE_VAL, IR_q, MEM_DATA, multiplexer_2_out,
       multiplexer_3_out, multiplexer_4_out, multiplexer_6_out, multiplexer_7_out, PC_VALUE, R0, R1, R2, R3,
       R4, R5, R6, R7, Ra_q, Rb_q, READ_MEMORY, register_file_1_ra_val, register_file_1_rb_val, RM_VALUE,
       Ry_q, RZ_VALUE;

  Adder #(.width(32)) adder_1 (.a(PC_VALUE), .b(bit_extender_1_out), .out(adder_1_out));  // open: cin, cout
  assign bit_extender_1_out = {{31{1'b0}}, 1'b1};  // Bit_Extender bit_extender_1
  Register #(.width(32)) IR (.D(READ_MEMORY), .en(INTERRUPT), .Q(IR_q), .clk(STAGE_1), .clr(CLEAR_CU));
  Register #(.width(32)) PC (.D(adder_1_out), .en(INTERRUPT), .Q(PC_VALUE), .clk(STAGE_1), .clr(CLEAR_CU));
  Instruction_Register instruction_register_1 (
    .Instruction(IR_q), .Opcode(OPCODE), .Ri_Stored(RY_ADDRESS), .Rj_Op1(RA_ADDRESS), .Rk_Op2(RB_ADDRESS),
    .Immdeiate(instruction_register_1_immdeiate));
  Control_Unit control_unit_1 (
    .mem_data(EN_MEM_DATA), .rm(EN_RM), .s1(STAGE_1), .s2(STAGE_2), .imm(EN_IMMEDIATE), .s3(STAGE_3),
    .write(EN_WRITE), .s4(STAGE_4), .optype(OP_TYPE), .s5(STAGE_5), .OPCODE(OPCODE), .clear(CLEAR_CU),
    .inter(control_unit_1_inter));
  assign IMMEDIATE_VAL = {{16{1'b0}}, instruction_register_1_immdeiate};  // Bit_Extender bit_extender_2
  not not_1 (INTERRUPT, control_unit_1_inter);
  Multiplexer #(.enable("false")) multiplexer_1 (
    .in0(STAGE_5), .in1(Register_Trigger), .out(multiplexer_1_out), .sel(En_Hardcode));
  Register #(.width(32)) Ra (.D(register_file_1_ra_val), .en(INTERRUPT), .Q(Ra_q), .clk(STAGE_2), .clr(CLEAR_Reg));
  Multiplexer #(.width(32)) multiplexer_2 (
    .in0(Ry_q), .in1(Hardcoded_Reg_Val_32_bit), .out(multiplexer_2_out), .sel(En_Hardcode), .en(and_1_out));
  Register_File register_file_1 (
    .Ry_val(multiplexer_2_out), .Ry(multiplexer_5_out), .clk_5(multiplexer_1_out), .clear(CLEAR_REG_FILE),
    .Ra_val(register_file_1_ra_val), .Rb_val(register_file_1_rb_val), .Ra(RA_ADDRESS), .Rb(RB_ADDRESS),
    .R0_out(R0), .R1_out(R1), .R2_out(R2), .R3_out(R3), .R4_out(R4), .R5_out(R5), .R6_out(R6), .R7_out(R7),
    .Interrupt(and_1_out));
  ALU alu_1 (.Rz(alu_1_rz), .op_type(OP_TYPE), .Ra(Ra_q), .Rb(multiplexer_4_out), .INTERRUPT(INTERRUPT));
  Register #(.width(32)) Rz (.D(alu_1_rz), .en(INTERRUPT), .Q(RZ_VALUE), .clk(STAGE_3), .clr(CLEAR_Reg));
  Multiplexer #(.width(32)) multiplexer_3 (
    .in0(RZ_VALUE), .in1(READ_MEMORY), .out(multiplexer_3_out), .sel(EN_MEM_DATA), .en(INTERRUPT));
  Register #(.width(32)) Ry (.D(multiplexer_3_out), .en(INTERRUPT), .Q(Ry_q), .clk(STAGE_4), .clr(CLEAR_Reg));
  Register #(.width(32)) Rb (.D(register_file_1_rb_val), .en(INTERRUPT), .Q(Rb_q), .clk(STAGE_2), .clr(CLEAR_Reg));
  Multiplexer #(.width(32)) multiplexer_4 (
    .in0(Rb_q), .in1(IMMEDIATE_VAL), .out(multiplexer_4_out), .sel(EN_IMMEDIATE), .en(INTERRUPT));
  Multiplexer #(.width(3), .enable("false")) multiplexer_5 (
    .in0(RY_ADDRESS), .in1(Hardcoded_Reg_Add_3_bit), .out(multiplexer_5_out), .sel(En_Hardcode));
  and and_1 (and_1_out, INTERRUPT, not_2_out);
  not not_2 (not_2_out, EN_WRITE);
  Register #(.width(32)) Rm (.D(Rb_q), .en(EN_RM), .Q(RM_VALUE), .clk(STAGE_3), .clr(CLEAR_Reg));
  Button button_1 (.out(CLEAR_CU));
  and and_2 (and_2_out, or_1_out, INTERRUPT);
  or or_1 (or_1_out, STAGE_3, STAGE_4);
  Button button_2 (.out(CLEAR_REG_FILE));
  Button button_3 (.out(CLEAR_Reg));
  or or_2 (RESET_CLOCK, En_Hardcode, CLEAR_CU);
  Bit_Extender #(.in_width(32), .out_width(8)) bit_extender_3 (.in(multiplexer_6_out), .out(bit_extender_3_out));
  Multiplexer #(.width(32), .enable("false")) multiplexer_6 (
    .in0(PC_VALUE), .in1(RZ_VALUE), .out(multiplexer_6_out), .sel(and_2_out));
  Multiplexer #(.width(32), .enable("false")) multiplexer_7 (
    .in0(RM_VALUE), .in1(Hardcoded_Data_32_bit), .out(multiplexer_7_out), .sel(En_Hardcode));
  or or_3 (or_3_out, EN_WRITE, En_Hardcode);
  Button button_4 (.out(CLEAR_MEMORY));
  Multiplexer #(.width(8), .enable("false")) multiplexer_8 (
    .in0(bit_extender_3_out), .in1(Hardcoded_Address_8_bit), .out(MEM_ADDRESS), .sel(En_Hardcode));
  Multiplexer #(.width(32), .enable("false")) multiplexer_9 (
    .in1(multiplexer_7_out), .out(MEM_DATA), .sel(or_3_out));  // open: in0
  or or_4 (or_4_out, STAGE_3, STAGE_4);
  or or_5 (or_5_out, STAGE_4, Memory_Trigger);
  and and_3 (and_3_out, or_4_out, EN_WRITE);
  or or_6 (or_6_out, and_3_out, En_Hardcode);
  RAM #(.dataWidth(32), .bus("separate")) ram_1 (
    .addr(MEM_ADDRESS), .din(MEM_DATA), .data(READ_MEMORY), .str(or_6_out), .clk(or_5_out), .ld(not_3_out),
    .clr(CLEAR_MEMORY));  // open: sel
  not not_3 (not_3_out, or_6_out);
  Clock CLOCK (.out(CLOCK_out));
  Counter counter_1 (
    .main_clk(CLOCK_out), .reset_clk(RESET_CLOCK), .clk_1(STAGE_1), .clk_2(STAGE_2), .clk_3(STAGE_3),
    .clk_4(STAGE_4), .clk_5(STAGE_5));
  Hex_Digit_Display hex_digit_display_1 (.value(R0[31:28]));  // open: dp
  Hex_Digit_Display hex_digit_display_2 (.value(R0[27:24]));  // open: dp
  Hex_Digit_Display hex_digit_display_3 (.value(R2[31:28]));  // open: dp
  Hex_Digit_Display hex_digit_display_4 (.value(R2[27:24]));  // open: dp
  Hex_Digit_Display hex_digit_display_5 (.value(R4[27:24]));  // open: dp
  Hex_Digit_Display hex_digit_display_6 (.value(R4[31:28]));  // open: dp
  Hex_Digit_Display hex_digit_display_7 (.value(R6[27:24]));  // open: dp
  Hex_Digit_Display hex_digit_display_8 (.value(R6[31:28]));  // open: dp
  Hex_Digit_Display hex_digit_display_9 (.value(R0[19:16]));  // open: dp
  Hex_Digit_Display hex_digit_display_10 (.value(R0[23:20]));  // open: dp
  Hex_Digit_Display hex_digit_display_11 (.value(R2[19:16]));  // open: dp
  Hex_Digit_Display hex_digit_display_12 (.value(R2[23:20]));  // open: dp
  Hex_Digit_Display hex_digit_display_13 (.value(R4[19:16]));  // open: dp
  Hex_Digit_Display hex_digit_display_14 (.value(R4[23:20]));  // open: dp
  Hex_Digit_Display hex_digit_display_15 (.value(R6[19:16]));  // open: dp
  Hex_Digit_Display hex_digit_display_16 (.value(R6[23:20]));  // open: dp
  Hex_Digit_Display hex_digit_display_17 (.value(R0[11:8]));  // open: dp
  Hex_Digit_Display hex_digit_display_18 (.value(R0[15:12]));  // open: dp
  Hex_Digit_Display hex_digit_display_19 (.value(R2[11:8]));  // open: dp
  Hex_Digit_Display hex_digit_display_20 (.value(R2[15:12]));  // open: dp
  Hex_Digit_Display hex_digit_display_21 (.value(R4[15:12]));  // open: dp
  Hex_Digit_Display hex_digit_display_22 (.value(R4[11:8]));  // open: dp
  Hex_Digit_Display hex_digit_display_23 (.value(R6[11:8]));  // open: dp
  Hex_Digit_Display hex_digit_display_24 (.value(R6[15:12]));  // open: dp
  Hex_Digit_Display hex_digit_display_25 (.value(R0[7:4]));  // open: dp
  Hex_Digit_Display hex_digit_display_26 (.value(R0[3:0]));  // open: dp
  Hex_Digit_Display hex_digit_display_27 (.value(R2[3:0]));  // open: dp
  Hex_Digit_Display hex_digit_display_28 (.value(R2[7:4]));  // open: dp
  Hex_Digit_Display hex_digit_display_29 (.value(R4[3:0]));  // open: dp
  Hex_Digit_Display hex_digit_display_30 (.value(R4[7:4]));  // open: dp
  Hex_Digit_Display hex_digit_display_31 (.value(R6[7:4]));  // open: dp
  Hex_Digit_Display hex_digit_display_32 (.value(R6[3:0]));  // open: dp
  Hex_Digit_Display hex_digit_display_33 (.value(R1[31:28]));  // open: dp
  Hex_Digit_Display hex_digit_display_34 (.value(R3[31:28]));  // open: dp
  Hex_Digit_Display hex_digit_display_35 (.value(R5[31:28]));  // open: dp
  Hex_Digit_Display hex_digit_display_36 (.value(R7[31:28]));  // open: dp
  Hex_Digit_Display hex_digit_display_37 (.value(R1[27:24]));  // open: dp
  Hex_Digit_Display hex_digit_display_38 (.value(R1[23:20]));  // open: dp
  Hex_Digit_Display hex_digit_display_39 (.value(R3[23:20]));  // open: dp
  Hex_Digit_Display hex_digit_display_40 (.value(R3[27:24]));  // open: dp
  Hex_Digit_Display hex_digit_display_41 (.value(R5[27:24]));  // open: dp
  Hex_Digit_Display hex_digit_display_42 (.value(R5[23:20]));  // open: dp
  Hex_Digit_Display hex_digit_display_43 (.value(R7[23:20]));  // open: dp
  Hex_Digit_Display hex_digit_display_44 (.value(R7[27:24]));  // open: dp
  Hex_Digit_Display hex_digit_display_45 (.value(R1[15:12]));  // open: dp
  Hex_Digit_Display hex_digit_display_46 (.value(R1[19:16]));  // open: dp
  Hex_Digit_Display hex_digit_display_47 (.value(R3[15:12]));  // open: dp
  Hex_Digit_Display hex_digit_display_48 (.value(R3[19:16]));  // open: dp
  Hex_Digit_Display hex_digit_display_49 (.value(R5[19:16]));  // open: dp
  Hex_Digit_Display hex_digit_display_50 (.value(R5[15:12]));  // open: dp
  Hex_Digit_Display hex_digit_display_51 (.value(R7[19:16]));  // open: dp
  Hex_Digit_Display hex_digit_display_52 (.value(R7[15:12]));  // open: dp
  Hex_Digit_Display hex_digit_display_53 (.value(R1[11:8]));  // open: dp
  Hex_Digit_Display hex_digit_display_54 (.value(R1[7:4]));  // open: dp
  Hex_Digit_Display hex_digit_display_55 (.value(R3[11:8]));  // open: dp
  Hex_Digit_Display hex_digit_display_56 (.value(R3[7:4]));  // open: dp
  Hex_Digit_Display hex_digit_display_57 (.value(R5[11:8]));  // open: dp
  Hex_Digit_Display hex_digit_display_58 (.value(R5[7:4]));  // open: dp
  Hex_Digit_Display hex_digit_display_59 (.value(R7[11:8]));  // open: dp
  Hex_Digit_Display hex_digit_display_60 (.value(R7[7:4]));  // open: dp
  Hex_Digit_Display hex_digit_display_61 (.value(R1[3:0]));  // open: dp
  Hex_Digit_Display hex_digit_display_62 (.value(R3[3:0]));  // open: dp
  Hex_Digit_Display hex_digit_display_63 (.value(R5[3:0]));  // open: dp
  Hex_Digit_Display hex_digit_display_64 (.value(R7[3:0]));  // open: dp

  // Other names for the same wires on the sheet: CLEAR_PC = CLEAR_CU; CLEAR_Ry = CLEAR_Reg;
  //   HARDCODED_ADDRESS[7:0] = Hardcoded_Address_8_bit; HARDCODED_DATA[31:0] = Hardcoded_Data_32_bit;
  //   HARDCODED_REG_ADD[2:0] = Hardcoded_Reg_Add_3_bit; HARDCODED_REG_VAL[31:0] = Hardcoded_Reg_Val_32_bit;
  //   MEM_TRIGGER = Memory_Trigger; Reg_TRIGGER = Register_Trigger

  // Notes on the sheet:
  //   Fetch Unit
  //   Control Unit
  //   5 Stage Pipeline
  //   Clear Buttons
  //   Processor memory interface
  //   Memory Unit
  //   Harcoded input
  //   Stage Counter
  //   MOV - 0
  //   MVI - 1
  //   LOAD - 2
  //   STORE - 3
  //   ADD - 4
  //   ADI - 5
  //   SUB - 6
  //   Register File Values - Only for visuals
  //   Opcode   Ry   Ra  Rb  Immediate
  //   Opcodes for different instructions:- 
  //   SUI - 7
  //   AND - 8
  //   ANI - 9
  //   OR - 10
  //   ORI - 11
  //   HLT - 12
endmodule

module Register_File (
  input  [2:0] Ra,
  input  Interrupt,
  input  [2:0] Ry,
  input  [2:0] Rb,
  input  [31:0] Ry_val,
  input  clk_5,
  input  clear,
  output [31:0] Ra_val,
  output [31:0] Rb_val,
  output [31:0] R0_out,
  output [31:0] R4_out,
  output [31:0] R1_out,
  output [31:0] R5_out,
  output [31:0] R2_out,
  output [31:0] R6_out,
  output [31:0] R3_out,
  output [31:0] R7_out
);

  wire demultiplexer_1_out0, demultiplexer_1_out1, demultiplexer_1_out2, demultiplexer_1_out3,
       demultiplexer_1_out4, demultiplexer_1_out5, demultiplexer_1_out6, demultiplexer_1_out7,
       multiplexer_1_out;

  Multiplexer #(.enable("false")) multiplexer_1 (.in0(1'b0), .in1(1'b1), .out(multiplexer_1_out), .sel(Interrupt));
  Demultiplexer #(.select(3), .enable("false")) demultiplexer_1 (
    .out0(demultiplexer_1_out0), .out1(demultiplexer_1_out1), .out2(demultiplexer_1_out2),
    .out3(demultiplexer_1_out3), .out4(demultiplexer_1_out4), .out5(demultiplexer_1_out5),
    .out6(demultiplexer_1_out6), .out7(demultiplexer_1_out7), .in(multiplexer_1_out), .sel(Ry));
  Register #(.width(32)) R0 (.D(Ry_val), .en(demultiplexer_1_out0), .Q(R0_out), .clk(clk_5), .clr(clear));
  Register #(.width(32)) R1 (.D(Ry_val), .en(demultiplexer_1_out1), .Q(R1_out), .clk(clk_5), .clr(clear));
  Register #(.width(32)) R2 (.D(Ry_val), .en(demultiplexer_1_out2), .Q(R2_out), .clk(clk_5), .clr(clear));
  Register #(.width(32)) R3 (.D(Ry_val), .en(demultiplexer_1_out3), .Q(R3_out), .clk(clk_5), .clr(clear));
  Register #(.width(32)) R4 (.D(Ry_val), .en(demultiplexer_1_out4), .Q(R4_out), .clk(clk_5), .clr(clear));
  Register #(.width(32)) R5 (.D(Ry_val), .en(demultiplexer_1_out5), .Q(R5_out), .clk(clk_5), .clr(clear));
  Register #(.width(32)) R6 (.D(Ry_val), .en(demultiplexer_1_out6), .Q(R6_out), .clk(clk_5), .clr(clear));
  Register #(.width(32)) R7 (.D(Ry_val), .en(demultiplexer_1_out7), .Q(R7_out), .clk(clk_5), .clr(clear));
  Multiplexer #(.select(3), .width(32)) multiplexer_2 (
    .in0(R0_out), .in1(R1_out), .in2(R2_out), .in3(R3_out), .in4(R4_out), .in5(R5_out), .in6(R6_out),
    .in7(R7_out), .out(Ra_val), .sel(Ra), .en(1'b1));
  Multiplexer #(.select(3), .width(32)) multiplexer_3 (
    .in0(R0_out), .in1(R1_out), .in2(R2_out), .in3(R3_out), .in4(R4_out), .in5(R5_out), .in6(R6_out),
    .in7(R7_out), .out(Rb_val), .sel(Rb), .en(1'b1));

  // Notes on the sheet:
  //   For showing register values in main
endmodule

module ALU (
  input  [31:0] Ra,
  input  [31:0] Rb,
  input  INTERRUPT,
  input  [2:0] op_type,
  output [31:0] Rz
);

  wire [31:0] adder_1_out, and_1_out, or_1_out, subtractor_1_out;

  Adder #(.width(32)) adder_1 (.a(Ra), .b(Rb), .out(adder_1_out));  // open: cin, cout
  Subtractor #(.width(32)) subtractor_1 (.a(Ra), .b(Rb), .out(subtractor_1_out));  // open: bin, bout
  assign and_1_out = Ra & Rb;  // AND_Gate and_1, 32 bits wide
  assign or_1_out = Ra | Rb;  // OR_Gate or_1, 32 bits wide
  Multiplexer #(.select(3), .width(32)) multiplexer_1 (
    .in0(Ra), .in1(adder_1_out), .in2(subtractor_1_out), .in3(and_1_out), .in4(or_1_out), .in5(Rb), .out(Rz),
    .sel(op_type), .en(INTERRUPT));  // open: in6, in7
endmodule

module Control_Unit (
  input  s1,
  input  s2,
  input  s3,
  input  s4,
  input  s5,
  input  clear,
  input  [3:0] OPCODE,
  output mem_data,
  output rm,
  output imm,
  output write,
  output [2:0] optype,
  output inter
);

  wire ADD, ADI, AND, ANI, decoder_1_out12, decoder_1_out13, decoder_1_out14, decoder_1_out15, EN_IMMEDIATE,
       EN_MEM_DATA, EN_RM, HLT, MOI, MOV, OR, or_3_out, or_4_out, or_5_out, or_6_out, ORI, SUB, SUI;
  wire [2:0] ANDOP, BBP, MINUS, OROP, PLUS;

  Decoder #(.select(4)) decoder_1 (
    .out0(MOV), .out1(MOI), .out2(EN_MEM_DATA), .out3(EN_RM), .out4(ADD), .out5(ADI), .out6(SUB), .out7(SUI),
    .out8(AND), .out9(ANI), .out10(OR), .out11(ORI), .out12(decoder_1_out12), .out13(decoder_1_out13),
    .out14(decoder_1_out14), .out15(decoder_1_out15), .sel(OPCODE));  // open: en
  or or_1 (EN_IMMEDIATE, MOI, EN_MEM_DATA, EN_RM, ADI, SUI, ANI, ORI);
  or or_2 (HLT, decoder_1_out12, decoder_1_out13, decoder_1_out14, decoder_1_out15);
  or or_3 (or_3_out, EN_MEM_DATA, EN_RM, ADD, ADI);
  or or_4 (or_4_out, SUB, SUI);
  Multiplexer #(.width(3), .enable("false")) multiplexer_1 (.in0(3'b000), .in1(3'b001), .out(PLUS), .sel(or_3_out));
  Multiplexer #(.width(3), .enable("false")) multiplexer_2 (.in0(3'b000), .in1(3'b010), .out(MINUS), .sel(or_4_out));
  or or_5 (or_5_out, OR, ORI);
  Multiplexer #(.width(3), .enable("false")) multiplexer_3 (.in0(3'b000), .in1(3'b011), .out(ANDOP), .sel(or_6_out));
  or or_6 (or_6_out, AND, ANI);
  Multiplexer #(.width(3), .enable("false")) multiplexer_4 (.in0(3'b000), .in1(3'b100), .out(OROP), .sel(or_5_out));
  Multiplexer #(.enable("false")) multiplexer_5 (.in0(EN_MEM_DATA), .in1(1'b0), .out(mem_data), .sel(clear));
  Multiplexer #(.enable("false")) multiplexer_6 (.in0(EN_RM), .in1(1'b0), .out(rm), .sel(clear));
  Multiplexer #(.enable("false")) multiplexer_7 (.in0(EN_IMMEDIATE), .in1(1'b0), .out(imm), .sel(clear));
  Multiplexer #(.enable("false")) multiplexer_8 (.in0(EN_RM), .in1(1'b0), .out(write), .sel(clear));
  Multiplexer #(.enable("false")) multiplexer_9 (.in0(HLT), .in1(1'b0), .out(inter), .sel(clear));
  Multiplexer #(.width(3), .enable("false")) multiplexer_10 (.in0(3'b000), .in1(3'b101), .out(BBP), .sel(MOI));
  assign optype = ANDOP | PLUS | MINUS | BBP | OROP;  // OR_Gate or_7, 3 bits wide

  // Other names for the same wires on the sheet: INTERRUPT = HLT; LOAD = EN_MEM_DATA; OP_TYPE[2:0] = optype;
  //   STAGE_1 = s1; STAGE_2 = s2; STAGE_3 = s3; STAGE_4 = s4; STAGE_5 = s5; EN_WRITE = EN_RM; STORE = EN_RM

  // Notes on the sheet:
  //   Decode Unit
  //   Input
  //   Output
endmodule

module Instruction_Register (
  input  [31:0] Instruction,
  output [3:0] Opcode,
  output [2:0] Ri_Stored,
  output [2:0] Rj_Op1,
  output [2:0] Rk_Op2,
  output [15:0] Immdeiate
);


  assign Immdeiate = Instruction[15:0];
  assign Opcode = Instruction[31:28];
  assign Ri_Stored = Instruction[26:24];
  assign Rj_Op1 = Instruction[22:20];
  assign Rk_Op2 = Instruction[18:16];

  // Other names for the same wires on the sheet: Immediate[15:0] = Instruction[15:0]; Ri[2:0] = Instruction[26:24];
  //   Rj[2:0] = Instruction[22:20]; Rk[2:0] = Instruction[18:16]
endmodule

module Counter (
  input  main_clk,
  input  reset_clk,
  output clk_1,
  output clk_2,
  output clk_3,
  output clk_4,
  output clk_5
);

  wire j_k_ff_1_q, j_k_ff_1_qn, j_k_ff_2_qn, j_k_ff_3_qn, j_k_ff_4_qn, j_k_ff_5_qn, j_k_ff_6_qn, or_1_out,
       or_2_out, or_3_out;

  or or_1 (or_1_out, clk_5, clk_4, clk_3, clk_2, clk_1);
  or or_2 (or_2_out, clk_5, j_k_ff_1_q);
  J_K_Flip_Flop j_k_ff_1 (
    .Q(j_k_ff_1_q), .Qn(j_k_ff_1_qn), .preset(reset_clk), .reset(or_1_out));  // open: J, clk, K, en
  or or_3 (or_3_out, j_k_ff_1_qn, j_k_ff_6_qn);
  J_K_Flip_Flop j_k_ff_2 (
    .J(or_2_out), .clk(main_clk), .K(or_3_out), .Q(clk_1), .Qn(j_k_ff_2_qn), .reset(reset_clk));  // open: preset, en
  J_K_Flip_Flop j_k_ff_3 (
    .J(clk_1), .clk(main_clk), .K(j_k_ff_2_qn), .Q(clk_2), .Qn(j_k_ff_3_qn), .reset(reset_clk));  // open: preset, en
  J_K_Flip_Flop j_k_ff_4 (
    .J(clk_2), .clk(main_clk), .K(j_k_ff_3_qn), .Q(clk_3), .Qn(j_k_ff_4_qn), .reset(reset_clk));  // open: preset, en
  J_K_Flip_Flop j_k_ff_5 (
    .J(clk_3), .clk(main_clk), .K(j_k_ff_4_qn), .Q(clk_4), .Qn(j_k_ff_5_qn), .reset(reset_clk));  // open: preset, en
  J_K_Flip_Flop j_k_ff_6 (
    .J(clk_4), .clk(main_clk), .K(j_k_ff_5_qn), .Q(clk_5), .Qn(j_k_ff_6_qn), .reset(reset_clk));  // open: preset, en

  // Notes on the sheet:
  //   Ring Counter
endmodule
